# Fritzing sketch Circuit Diagram - Final Project (saved by Fritzing 0.9.5d)
breadboards: 1

parts:
  Part1 = Arduino Uno (Rev3)
  LED1 = LED - 5mm [color="Red (633nm)" package="5 mm [THT]"]
  LED2 = LED - 5mm [color="Red (633nm)" package="5 mm [THT]"]
  LED3 = LED - 5mm [color="Red (633nm)" package="5 mm [THT]"]
  LED4 = LED - 5mm [color="Red (633nm)" package="5 mm [THT]"]
  LED5 = LED - 5mm [color="Red (633nm)" package="5 mm [THT]"]
  LED6 = LED - 5mm [color="Red (633nm)" package="5 mm [THT]"]
  LED7 = LED - 5mm [color="Red (633nm)" package="5 mm [THT]"]
  S1 = Pushbutton [package="[THT]"]
  S2 = Pushbutton [package="[THT]"]
  S3 = Pushbutton [package="[THT]"]
  S4 = Pushbutton [package="[THT]"]
  R1 = Resistor [tolerance=±5% resistance=220 package=THT]
  R2 = Resistor [tolerance=±5% resistance=220 package=THT]
  R3 = Resistor [tolerance=±5% resistance=220 package=THT]
  R4 = Resistor [tolerance=±5% resistance=220 package=THT]
  R5 = Resistor [tolerance=±5% resistance=220 package=THT]
  R6 = Resistor [tolerance=±5% resistance=220 package=THT]
  R7 = Resistor [tolerance=±5% resistance=220 package=THT]
  J1 = Piezo Speaker

nets:
  N1: Part1.D8, LED7.anode
  N2: Part1.D9_PWM, S3.Pin_1, S3.Pin_2
  N3: Part1.D10_PWM/SS, S2.Pin_1, S2.Pin_2
  N4: Part1.D11_PWM/MOSI, S1.Pin_1, S1.Pin_2
  N5: Part1.D12/MISO, S4.Pin_1, S4.Pin_2
  N6: Part1.D13/SCK, J1.pin2
  N7: Part1.GND, S1.Pin_3, S1.Pin_4, S2.Pin_3, S2.Pin_4, S3.Pin_3, S3.Pin_4, S4.Pin_3, S4.Pin_4, R1.Pin_1, R2.Pin_1, R3.Pin_1, R4.Pin_1, R5.Pin_1, R6.Pin_1, R7.Pin_1, J1.pin1
  N8: Part1.D2, LED1.anode
  N9: Part1.D3_PWM, LED2.anode
  N10: Part1.D5_PWM, LED4.anode
  N11: Part1.D6_PWM, LED5.anode
  N12: Part1.D7, LED6.anode
  N13: LED1.cathode, R1.Pin_0
  N14: LED2.cathode, R2.Pin_0
  N15: LED3.cathode, R4.Pin_0
  N16: LED4.cathode, R3.Pin_0
  N17: LED5.cathode, R5.Pin_0
  N18: LED6.cathode, R6.Pin_0
  N19: LED7.cathode, R7.Pin_0
